# Fritzing sketch ArduinoUNO_LCD (saved by Fritzing 0.9.3b)
breadboards: 1

parts:
  LCD1 = LCD screen
  Часть1 = Arduino Uno (Rev3) - ICSP
  S1 = Momentary Switch [package=ksa_sealed_tac_switch]
  S2 = Momentary Switch [package=ksa_sealed_tac_switch]
  LED1 = RGB LED - (4 legs) [package="5 mm [THT]"]
  R1 = Resistor [tolerance=±5% resistance=220 package=THT]
  R2 = Resistor [tolerance=±5% resistance=220 package=THT]
  R3 = Resistor [tolerance=±5% resistance=220 package=THT]

nets:
  VSS: LCD1.VSS, LCD1.V0, LCD1.R/W, LCD1.LED-, Часть1.GND, S1.1, S1.2, S2.1, S2.2, LED1.common_anode
  VDD: LCD1.VDD, LCD1.LED+, Часть1.5V
  N1: LCD1.RS, Часть1.D4
  N2: LCD1.E, Часть1.D5_PWM
  N3: LCD1.DB4, Часть1.D9_PWM
  N4: LCD1.DB5, Часть1.D10_PWM/SS
  N5: LCD1.DB6, Часть1.D11_PWM/MOSI
  N6: LCD1.DB7, Часть1.D12/MISO
  N7: Часть1.A0, R3.Pin_0
  N8: Часть1.A1, R2.Pin_0
  N9: Часть1.A2, R1.Pin_0
  N10: Часть1.D2, S1.3, S1.4
  N11: Часть1.D3_PWM, S2.3, S2.4
  N12: LED1.red_cathode, R3.Pin_1
  N13: LED1.green_cathode, R2.Pin_1
  N14: LED1.blue_cathode, R1.Pin_1
